# Fritzing sketch wiring (saved by Fritzing 0.9.3b)
breadboards: 1

parts:
  Raspberry_Pi_1 = Raspberry Pi 3 [part_number=RPI-3-V1.2]
  M2 = DC Motor
  M3 = DC Motor
  S1 = H-Bridge with L298N
  VCC1 = 4 x AAA Battery Mount

nets:
  N1: Raspberry_Pi_1.GIPO4, S1.IN1
  N2: Raspberry_Pi_1.GIPO17, S1.IN2
  N3: Raspberry_Pi_1.GIPO27, S1.IN3
  N4: Raspberry_Pi_1.GIPO22, S1.IN4
  GND: Raspberry_Pi_1.GND, S1.GND
  5V: Raspberry_Pi_1.5V, S1.5V
  N5: M2.pin_1, S1.M2-01
  N6: M2.pin_2, S1.M2-02
  N7: M3.pin_1, S1.M1-02
  N8: M3.pin_2, S1.M1-01
  N9: S1.12V, VCC1.+

custom parts:
  H-Bridge with L298N: h-bridge
